// Logisim project SAP1-Fibonacci-Div.circ as structural Verilog: 13 circuits, main circuit main
module main (
  input  Reset,
  output [3:0] Dados,
  output [3:0] \Dados___Endereços ,
  output out_4,
  output out_5,
  output out_6,
  output out_7,
  output out_8,
  output out_9,
  output out_10,
  output out_11
);

  wire CLK, Clock_out, Cp, Dec, Div, Ea, Eb, Ep, Eq, Eu, Gr, Inc, Lo, Lp, Mul, nCE, nEi, nLa, nLb, nLi, nLm,
       nLo, not_1_out, not_2_out, not_3_out, not_4_out, \registrador_instruções_1_i4 ,
       \registrador_instruções_1_i5 , \registrador_instruções_1_i6 , \registrador_instruções_1_i7 ,
       rom_1_hlt, Su, Sv;
  wire [3:0] rem_1_remout;
  wire [7:0] acumulador_1_a_out_ula, counter_1_q, registrador_b_1_b_dataout;

  Clock Clock (.out(Clock_out));
  not not_1 (not_1_out, CLK);
  not not_2 (not_2_out, Reset);
  not not_3 (not_3_out, nCE);
  assign CLK = not_4_out ? Clock_out : 1'bz;  // Controlled_Buffer controlled_buffer_1
  not not_4 (not_4_out, rom_1_hlt);
  REM rem_1 (.in_1(\Dados___Endereços ), .nLm(nLm), .CLK(CLK), .REMOut(rem_1_remout));
  Contador_Programa contador_programa_1 (
    .Cp(Cp), .nCLK(not_1_out), .nCLR(not_2_out), .Ep(Ep), .Cp_Out(\Dados___Endereços ), .Lp(Lp),
    .Cp_In(\Dados___Endereços ));
  \Memória_RAM  \memória_ram_1  (
    .out_6({Dados, \Dados___Endereços }), .in_1(rem_1_remout), .in_2({Dados, \Dados___Endereços }),
    .nCE(not_3_out), .CLK(CLK), .Sv(Sv));
  \Registrador_Instruções  \registrador_instruções_1  (
    .in_1({Dados, \Dados___Endereços }), .nLi(nLi), .CLK(CLK), .CLR(Reset), .nEi(nEi),
    .out_6({Dados, \Dados___Endereços }), .I4(\registrador_instruções_1_i4 ),
    .I5(\registrador_instruções_1_i5 ), .I6(\registrador_instruções_1_i6 ), .I7(\registrador_instruções_1_i7 ));
  ROM rom_1 (
    .CLK(CLK), .CLR(Reset), .HLT(rom_1_hlt), .Cp(Cp), .Ep(Ep), .nLm(nLm), .nCE(nCE), .nLl(nLi), .nEl(nEi),
    .nLa(nLa), .Ea(Ea), .Su(Su), .Eu(Eu), .nLb(nLb), .nLo(nLo), .I7(\registrador_instruções_1_i7 ),
    .I6(\registrador_instruções_1_i6 ), .I4(\registrador_instruções_1_i4 ), .Inc(Inc), .Dec(Dec), .Mul(Mul),
    .Eq(Eq), .I5(\registrador_instruções_1_i5 ), .Eb(Eb), .Sv(Sv), .Lp(Lp), .Lo(Lo), .Div(Div), .Gr(Gr));
  Acumulador acumulador_1 (
    .A_In({Dados, \Dados___Endereços }), .nLa(nLa), .CLK(CLK), .Ea(Ea), .A_Out_ULA(acumulador_1_a_out_ula),
    .A_Out({Dados, \Dados___Endereços }));
  Somador_Subtrator somador_subtrator_1 (
    .Su(Su), .B_data(registrador_b_1_b_dataout), .A_dataOut2({Dados, \Dados___Endereços }),
    .A_data(acumulador_1_a_out_ula), .Eu(Eu), .Gr(Gr), .Lo(Lo), .Eq(Eq), .Mu(Mul), .Dv(Div), .inc(Inc),
    .dec(Dec));
  Registrador_B registrador_b_1 (
    .B_dataIn({Dados, \Dados___Endereços }), .B_dataOut(registrador_b_1_b_dataout), .nLb(nLb), .CLK(CLK));
  Hex_Digit_Display hex_digit_display_1 (.value({out_4, out_5, out_6, out_7}));  // open: dp
  \Indicação_Visual  \indicação_visual_1  (
    .Input({Dados, \Dados___Endereços }),
    .Output({out_4, out_5, out_6, out_7, out_8, out_9, out_10, out_11}), .nLo(nLo), .CLK(CLK), .CLR(Reset));
  DotMatrix #(.matrixcols(8), .matrixrows(1), .dotshape("circle")) dotmatrix_1 (
    .col0(out_4), .col1(out_5), .col2(out_6), .col3(out_7), .col4(out_8), .col5(out_9), .col6(out_10),
    .col7(out_11));
  Hex_Digit_Display hex_digit_display_2 (.value({out_8, out_9, out_10, out_11}));  // open: dp
  Counter #(.behavior("old")) counter_1 (
    .Q(counter_1_q), .clk(CLK), .clr(Reset));  // open: load, D, count, carry, preset
  Hex_Digit_Display hex_digit_display_3 (.value(counter_1_q[7:4]));  // open: dp
  Hex_Digit_Display hex_digit_display_4 (.value(counter_1_q[3:0]));  // open: dp

  // Other names for the same wires on the sheet: CLR = Reset

  // Notes on the sheet:
  //   SAP-1 EM LOGISIM Modificado Cláudio Ver2/2024
  //   Arquitetura de Computadores I
  //   Instruções:
  //   LDA 0000: A<-*(MEM)
  //   ADD 0001: A<-A+B
  //   SUB 0010: A<-A-B
  //   INC 0011: A<=A+1
  //   DEC 0100: A<=A-1
  //   MUL 0101: A<-AxB
  //   JMP 0110: CP<-endereço de salto
  //   DIV 0111: A<= A/B
  //   OUT 1110: exibir o valor
  //   HLT 1111: interromper o circuito
  //   Fibonacci :
  //   Como usar:
  //   Adicione as operações no bloco de memória RAM,
  //   execute um RESET e envie pulsos de clock.
  //   Grupo:
  //   - Paulo Henrique Lopes de Paula
  //   - Douglas Nicolas Silva Gomes
  //   - Henrique Augusto de Oliveira Marcelino
  //   - Vitor de Meira Gomes
  //   0f 1e e0 be 1f e0 bf 60 00 00 00 00 00 00 1 1
  //   SAVE 1011: *salva o valor do acumulador na memoria RAM*
endmodule

module Contador_Programa (
  input  Lp,
  input  [3:0] Cp_In,
  input  Cp,
  input  nCLK,
  input  nCLR,
  input  Ep,
  output [3:0] Cp_Out
);

  wire not_1_out;
  wire [3:0] counter_1_q;

  not not_1 (not_1_out, nCLR);
  Counter #(.width(4), .max('hf), .trigger("falling"), .behavior("old")) counter_1 (
    .load(Lp), .D(Cp_In), .count(Cp), .Q(counter_1_q), .clk(nCLK), .clr(not_1_out));  // open: carry, preset
  assign Cp_Out = Ep ? counter_1_q : 4'bz;  // Controlled_Buffer controlled_buffer_1
endmodule

module REM (
  input  [3:0] in_1,
  input  nLm,
  input  CLK,
  output [3:0] REMOut
);

  wire not_1_out;

  not not_1 (not_1_out, nLm);
  Register #(.width(4), .Select("low")) register_1 (.D(in_1), .en(not_1_out), .Q(REMOut), .clk(CLK));  // open: clr
endmodule

module \Memória_RAM  (
  input  [3:0] in_1,
  input  [7:0] in_2,
  input  nCE,
  input  CLK,
  input  Sv,
  output [7:0] out_6
);

  wire and_1_out, not_1_out, or_1_out;
  wire [7:0] ram_1_data;

  or or_1 (or_1_out, Sv, nCE);
  RAM #(.addrWidth(4), .Select("high"), .simpleMode("false")) ram_1 (
    .addr(in_1), .data(ram_1_data), .sel(or_1_out), .clk(CLK), .ld(and_1_out));  // open: clr
  and and_1 (and_1_out, nCE, not_1_out);
  not not_1 (not_1_out, Sv);
  assign out_6 = nCE ? ram_1_data : 8'bz;  // Controlled_Buffer controlled_buffer_1
  assign ram_1_data = Sv ? in_2 : 8'bz;  // Controlled_Buffer controlled_buffer_2

  // Notes on the sheet:
  //   Operações:
  //   Exemplo 1:  02 + 03 - 04 + 02 = 03
  //   0f e0 1e e0 2d e0 1f e0 f0 00 00 00 00 04 03 02
  //   Exemplo 2:  150 + 70 - 50 + 100 = ? 270
  //   0f e0 1e e0 2d e0 1c e0 f0 00 00 00 64 32 46 96
  //   Exemplo 3:  5 x 2 - 1 - 2 + 1 = 8
  //   0f e0 5e e0 40 e0 2e e0 30 e0 f0 00 00 00 02 05
  //   Exemplo 4:  Carrega A=1,Exibe A, Inc A, Exibe A, JMP para Inc A 
  //   0f e0 30 e0 62 f0
  //   Exemplo 5:  15 + 5 / 2 + 7
  //   0f e0 1e e0 7d e0 1c e0 00 00 00 00 07 02 05 0f
  //   Fibonacci:
  //   0f 1e e0 be 1f e0 bf 60 00 00 00 00 00 00 1 1
endmodule

module \Registrador_Instruções  (
  input  [7:0] in_1,
  input  nLi,
  input  CLK,
  input  CLR,
  input  nEi,
  output [7:0] out_6,
  output I4,
  output I5,
  output I6,
  output I7
);

  wire not_1_out, not_2_out;
  wire [3:0] register_1_q;
  wire [7:0] bit_extender_1_out;

  not not_1 (not_1_out, nLi);
  not not_2 (not_2_out, nEi);
  Register #(.Select("low")) register_1 (
    .D(in_1), .en(not_1_out), .Q({I7, I6, I5, I4, register_1_q}), .clk(CLK), .clr(CLR));
  assign bit_extender_1_out = {{4{1'b0}}, register_1_q};  // Bit_Extender bit_extender_1
  assign out_6 = not_2_out ? bit_extender_1_out : 8'bz;  // Controlled_Buffer controlled_buffer_1
endmodule

module Acumulador (
  input  [7:0] A_In,
  input  nLa,
  input  CLK,
  input  Ea,
  output [7:0] A_Out_ULA,
  output [7:0] A_Out
);

  wire not_1_out;

  not not_1 (not_1_out, nLa);
  Register #(.Select("low")) register_1 (.D(A_In), .en(not_1_out), .Q(A_Out_ULA), .clk(CLK));  // open: clr
  assign A_Out = Ea ? A_Out_ULA : 8'bz;  // Controlled_Buffer controlled_buffer_1
endmodule

module Somador_Subtrator (
  input  Su,
  input  inc,
  input  dec,
  input  [7:0] B_data,
  input  [7:0] A_data,
  input  Eu,
  input  Gr,
  input  Lo,
  input  Eq,
  input  Mu,
  input  Dv,
  output [7:0] A_dataOut2
);

  wire comparator_1_eq, comparator_1_gt, comparator_1_lt, not_1_out, or_1_out;
  wire [7:0] adder_1_out, bit_extender_1_out, bit_extender_2_out, bit_extender_3_out,
       controlled_buffer_1_out, divider_1_out, multiplier_1_out, xor_1_out;

  or or_1 (or_1_out, inc, dec);
  not not_1 (not_1_out, or_1_out);
  assign controlled_buffer_1_out = not_1_out ? B_data : 8'bz;  // Controlled_Buffer controlled_buffer_1
  assign controlled_buffer_1_out = or_1_out ? 8'h1 : 8'bz;  // Controlled_Buffer controlled_buffer_2
  assign xor_1_out = {8{Su}} ^ controlled_buffer_1_out;  // XOR_Gate xor_1, 8 bits wide
  Adder adder_1 (.a(xor_1_out), .b(A_data), .out(adder_1_out), .cin(Su));  // open: cout
  Comparator comparator_1 (.a(A_data), .b(B_data), .gt(comparator_1_gt), .eq(comparator_1_eq), .lt(comparator_1_lt));
  assign A_dataOut2 = Mu ? multiplier_1_out : 8'bz;  // Controlled_Buffer controlled_buffer_3
  Multiplier multiplier_1 (.a(A_data), .b(B_data), .out(multiplier_1_out));  // open: cin, cout
  Divider divider_1 (.a(A_data), .b(B_data), .out(divider_1_out));  // open: upper, rem
  assign A_dataOut2 = Dv ? divider_1_out : 8'bz;  // Controlled_Buffer controlled_buffer_4
  assign A_dataOut2 = Eu ? adder_1_out : 8'bz;  // Controlled_Buffer controlled_buffer_5
  assign bit_extender_1_out = {{7{1'b0}}, comparator_1_gt};  // Bit_Extender bit_extender_1
  assign bit_extender_2_out = {{7{1'b0}}, comparator_1_eq};  // Bit_Extender bit_extender_2
  assign bit_extender_3_out = {{7{1'b0}}, comparator_1_lt};  // Bit_Extender bit_extender_3
  assign A_dataOut2 = Gr ? bit_extender_1_out : 8'bz;  // Controlled_Buffer controlled_buffer_6
  assign A_dataOut2 = Lo ? bit_extender_2_out : 8'bz;  // Controlled_Buffer controlled_buffer_7
  assign A_dataOut2 = Eq ? bit_extender_3_out : 8'bz;  // Controlled_Buffer controlled_buffer_8
endmodule

module Registrador_B (
  input  [7:0] B_dataIn,
  input  nLb,
  input  CLK,
  output [7:0] B_dataOut
);

  wire not_1_out;

  Register #(.Select("low")) register_1 (.D(B_dataIn), .en(not_1_out), .Q(B_dataOut), .clk(CLK));  // open: clr
  not not_1 (not_1_out, nLb);
endmodule

module Decodificador (
  input  l7,
  input  l6,
  input  l5,
  input  l4,
  output LDA,
  output ADD,
  output SUB,
  output OUT,
  output HLT
);

  wire and_1_out, and_2_out, and_3_out, and_4_out, and_5_out, not_1_out, not_2_out, not_3_out, not_4_out;

  not not_1 (not_1_out, l7);
  not not_2 (not_2_out, l6);
  not not_3 (not_3_out, l5);
  not not_4 (not_4_out, l4);
  buf buffer_1 (LDA, and_1_out);
  and and_1 (and_1_out, not_1_out, not_2_out, not_3_out, not_4_out);
  and and_2 (and_2_out, not_1_out, not_2_out, not_3_out, l4);
  buf buffer_2 (ADD, and_2_out);
  and and_3 (and_3_out, not_1_out, not_2_out, l5, not_4_out);
  buf buffer_3 (SUB, and_3_out);
  buf buffer_4 (OUT, and_4_out);
  and and_4 (and_4_out, l7, l6, l5, not_4_out);
  and and_5 (and_5_out, l7, l6, l5, l4);
  buf buffer_5 (HLT, and_5_out);
endmodule

module Fibonacci (
  input  Reset
);

  wire and_1_out, and_2_out, and_3_out, clock_1_out, controlled_buffer_1_out, controlled_buffer_2_out,
       controlled_buffer_3_out, controlled_buffer_4_out, controlled_buffer_5_out, controlled_buffer_7_out,
       counter_2_q, demultiplexer_1_out0, demultiplexer_1_out1, demultiplexer_1_out2, demultiplexer_2_out0,
       demultiplexer_2_out1, not_1_out, not_2_out, not_3_out, not_4_out, s_r_ff_1_q, s_r_ff_2_q, s_r_ff_3_q,
       s_r_ff_3_qn;
  wire [1:0] counter_1_q;
  wire [31:0] adder_1_out, controlled_buffer_8_out, R1_q, R2_q, Temp_q;

  Clock clock_1 (.out(clock_1_out));
  S_R_Flip_Flop #(.Pre_Clr_Positions("LEGACY"), .enable("true"), .NewFFLayout("false")) s_r_ff_1 (
    .Q(s_r_ff_1_q), .preset(Reset), .reset(and_3_out));  // open: S, clk, R, Qn, en
  and and_1 (and_1_out, clock_1_out, s_r_ff_2_q);
  S_R_Flip_Flop #(.Pre_Clr_Positions("LEGACY"), .enable("true"), .NewFFLayout("false")) s_r_ff_2 (
    .Q(s_r_ff_2_q), .preset(and_3_out), .reset(Reset));  // open: S, clk, R, Qn, en
  not not_1 (not_1_out, and_1_out);
  and and_2 (and_2_out, clock_1_out, s_r_ff_1_q);
  Demultiplexer #(.select(2), .disabled(0), .enable("false")) demultiplexer_1 (
    .out0(demultiplexer_1_out0), .out1(demultiplexer_1_out1), .out2(demultiplexer_1_out2), .in(and_2_out),
    .sel(counter_1_q));  // open: out3
  Counter #(.width(2), .max('h3), .behavior("old")) counter_1 (
    .Q(counter_1_q), .clk(not_2_out), .clr(Reset));  // open: load, D, count, carry, preset
  not not_2 (not_2_out, and_2_out);
  and and_3 (and_3_out, not_4_out, not_3_out);
  not not_3 (not_3_out, not_4_out);
  Demultiplexer #(.enable("false")) demultiplexer_2 (
    .out0(demultiplexer_2_out0), .out1(demultiplexer_2_out1), .in(and_1_out), .sel(counter_2_q));
  Counter #(.width(1), .max('h1)) counter_2 (
    .Q(counter_2_q), .clk(not_1_out), .clr(Reset));  // open: load, D, count, carry, preset, down
  assign controlled_buffer_1_out = demultiplexer_1_out0 ? demultiplexer_1_out0 : 1'bz;  // Controlled_Buffer controlled_buffer_1
  assign controlled_buffer_2_out = demultiplexer_1_out0 ? demultiplexer_1_out0 : 1'bz;  // Controlled_Buffer controlled_buffer_2
  assign controlled_buffer_3_out = demultiplexer_1_out1 ? demultiplexer_1_out1 : 1'bz;  // Controlled_Buffer controlled_buffer_3
  assign controlled_buffer_4_out = demultiplexer_1_out2 ? demultiplexer_1_out2 : 1'bz;  // Controlled_Buffer controlled_buffer_4
  not not_4 (not_4_out, demultiplexer_1_out2);
  assign controlled_buffer_5_out = demultiplexer_2_out0 ? demultiplexer_2_out0 : 1'bz;  // Controlled_Buffer controlled_buffer_5
  assign controlled_buffer_3_out = demultiplexer_2_out1 ? demultiplexer_2_out1 : 1'bz;  // Controlled_Buffer controlled_buffer_6
  assign controlled_buffer_7_out = demultiplexer_2_out1 ? demultiplexer_2_out1 : 1'bz;  // Controlled_Buffer controlled_buffer_7
  Pull_Resistor pull_resistor_1 (.node(controlled_buffer_2_out));
  Pull_Resistor pull_resistor_2 (.node(controlled_buffer_5_out));
  Pull_Resistor pull_resistor_3 (.node(controlled_buffer_4_out));
  Pull_Resistor pull_resistor_4 (.node(controlled_buffer_7_out));
  Pull_Resistor pull_resistor_5 (.node(controlled_buffer_3_out));
  Pull_Resistor pull_resistor_6 (.node(controlled_buffer_1_out));
  // Probe on R1_q
  assign controlled_buffer_8_out = s_r_ff_3_q ? Temp_q : 32'bz;  // Controlled_Buffer controlled_buffer_8
  assign controlled_buffer_8_out = s_r_ff_3_qn ? 32'h1 : 32'bz;  // Controlled_Buffer controlled_buffer_9
  S_R_Flip_Flop #(.Pre_Clr_Positions("LEGACY"), .enable("true"), .NewFFLayout("false")) s_r_ff_3 (
    .Q(s_r_ff_3_q), .Qn(s_r_ff_3_qn), .preset(controlled_buffer_4_out), .reset(controlled_buffer_2_out));  // open: S, clk, R, en
  Register #(.width(32), .Select("low")) R1 (
    .D(R2_q), .Q(R1_q), .clk(controlled_buffer_7_out), .clr(controlled_buffer_1_out));  // open: en
  Register #(.width(32), .Select("low")) R2 (
    .D(controlled_buffer_8_out), .Q(R2_q), .clk(controlled_buffer_3_out));  // open: en, clr
  Register #(.width(32), .Select("low")) Temp (
    .D(adder_1_out), .Q(Temp_q), .clk(controlled_buffer_5_out));  // open: en, clr
  Adder #(.width(32)) adder_1 (.a(R1_q), .b(R2_q), .out(adder_1_out));  // open: cin, cout
endmodule

module \Indicação_Visual  (
  input  [7:0] Input,
  input  nLo,
  input  CLK,
  input  CLR,
  output [7:0] Output
);

  wire not_1_out;

  not not_1 (not_1_out, nLo);
  Register #(.Select("low")) register_1 (.D(Input), .en(not_1_out), .Q(Output), .clk(CLK), .clr(CLR));
endmodule

module ROM (
  input  I7,
  input  I6,
  input  I5,
  input  I4,
  input  CLK,
  input  CLR,
  output Cp,
  output Ep,
  output nLm,
  output nCE,
  output nLl,
  output nEl,
  output nLa,
  output Ea,
  output Su,
  output Eu,
  output nLb,
  output nLo,
  output Inc,
  output Dec,
  output Mul,
  output Lp,
  output Eb,
  output Sv,
  output Eq,
  output Lo,
  output Div,
  output Gr,
  output HLT
);

  wire and_2_out, and_3_out, and_5_out, and_6_out, and_7_out, and_8_out, clr_t, load, nop, nor_1_out,
       not_1_out, not_2_out, or_1_out, shift_register_1_q0, shift_register_1_q1, shift_register_1_q3,
       shift_register_1_q4;
  wire [1:0] rom_2_data;
  wire [5:0] counter_1_q, rom_1_data;

  and and_1 (HLT, I7, I6, I5, I4);
  ROM_part #(.addrWidth(4), .dataWidth(6), .Select("high")) rom_1 (.addr({I7, I6, I5, I4}), .data(rom_1_data));
  or or_1 (or_1_out, CLR, nop);
  or or_2 (clr_t, or_1_out, nor_1_out);
  not not_1 (not_1_out, load);
  not not_2 (not_2_out, CLK);
  Shift_Register #(.length(6)) shift_register_1 (
    .in(nor_1_out), .clk(CLK), .clr(or_1_out), .q0(shift_register_1_q0), .q1(shift_register_1_q1), .q2(load),
    .q3(shift_register_1_q3), .q4(shift_register_1_q4));  // open: shift, out, load, d0, d1, d2, d3, d4, d5, q5
  Counter #(.width(6), .max('h3f), .ongoal("continue"), .behavior("old")) counter_1 (
    .load(load), .D(rom_1_data), .count(not_1_out), .Q(counter_1_q), .clk(not_2_out), .clr(clr_t));  // open: carry, preset
  nor nor_1 (nor_1_out, shift_register_1_q0, shift_register_1_q1, load, shift_register_1_q3, shift_register_1_q4);
  ROM_part #(.addrWidth(6), .dataWidth(24), .Select("high")) rom_2 (
    .addr(counter_1_q),
    .data({Cp, Ep, nLm, nCE, nLl, nEl, nLa, Ea, Su, Eu, nLb, nLo, Inc, Dec, Mul, Lp, Eb, Sv, Eq, Lo, Div, Gr, rom_2_data}));
  and and_2 (and_2_out, ~Cp, ~Ep, nLm, nCE);  // AND_Gate
  and and_3 (and_3_out, nLl, nEl, nLa, ~Ea);  // AND_Gate
  and and_4 (nop, and_2_out, and_3_out, and_5_out, and_6_out, and_7_out, and_8_out);
  and and_5 (and_5_out, ~Su, ~Eu, nLb, nLo);  // AND_Gate
  and and_6 (and_6_out, ~Inc, ~Dec, ~Mul, ~Lp);  // AND_Gate
  and and_7 (and_7_out, ~Eb, ~Sv, ~Eq, Lo);  // AND_Gate
  and and_8 (and_8_out, ~Div, ~Gr);  // AND_Gate

  // Notes on the sheet:
  //   contents of rom_1 (hex, n*v repeats v):
  //   3 6 9 10 13 16 19 1c 20 23 26 29 0 0 c
  //   contents of rom_2 (hex, n*v repeats v):
  //   5e3000 be3000 263000 1a3000 2c3000 3e3000 1a3000 2e1000 3c7000 1a3000 2e1000 3cf000 3f2000 3e3000
  //   3e3000 0 3c7800 3e3000 3e3000 3cf400 3e3000 3e3000 1a3000 2e1000 3c3200 3a3100 3e3000 3e3000 1a3000
  //   2e1000 3c3008 0 1a3000 2e1000 3c3004 1a3000 2e1000 3c3010 1a3000 2e1000 3c3020 263000 1a3000 3f3040
endmodule

module ContadorEmAnel (
  input  in_1,
  input  in_2,
  input  in_3,
  input  in_4,
  output out_5,
  output out_6,
  output out_7,
  output out_8,
  output out_9,
  output out_10
);

  wire or_1_out, or_2_out, or_3_out, or_4_out, or_5_out;

  D_Flip_Flop #(.Pre_Clr_Positions("LEGACY"), .enable("true"), .NewFFLayout("false")) d_ff_1 (
    .clk(in_1), .D(in_2), .Q(out_8), .preset(in_3), .en(1'b1), .reset(in_4));  // open: Qn
  D_Flip_Flop #(.Pre_Clr_Positions("LEGACY"), .enable("true"), .NewFFLayout("false")) d_ff_2 (
    .clk(in_1), .D(out_8), .Q(out_9), .en(1'b1), .reset(or_1_out));  // open: Qn, preset
  or or_1 (or_1_out, in_3, in_4);
  D_Flip_Flop #(.Pre_Clr_Positions("LEGACY"), .enable("true"), .NewFFLayout("false")) d_ff_3 (
    .clk(in_1), .D(out_9), .Q(out_10), .en(1'b1), .reset(or_2_out));  // open: Qn, preset
  or or_2 (or_2_out, in_3, in_4);
  D_Flip_Flop #(.Pre_Clr_Positions("LEGACY"), .enable("true"), .NewFFLayout("false")) d_ff_4 (
    .clk(in_1), .D(out_10), .Q(out_5), .en(1'b1), .reset(or_3_out));  // open: Qn, preset
  or or_3 (or_3_out, in_3, in_4);
  D_Flip_Flop #(.Pre_Clr_Positions("LEGACY"), .enable("true"), .NewFFLayout("false")) d_ff_5 (
    .clk(in_1), .D(out_5), .Q(out_6), .en(1'b1), .reset(or_4_out));  // open: Qn, preset
  or or_4 (or_4_out, in_3, in_4);
  D_Flip_Flop #(.Pre_Clr_Positions("LEGACY"), .enable("true"), .NewFFLayout("false")) d_ff_6 (
    .clk(in_1), .D(out_6), .Q(out_7), .en(1'b1), .reset(or_5_out));  // open: Qn, preset
  or or_5 (or_5_out, in_3, in_4);
endmodule
